// Digital circuit Ejercicio1.dig as structural Verilog
module Ejercicio1 (
  input  D3,
  input  D2,
  input  D1,
  input  D0,
  input  Sel2,
  input  Sel1,
  input  D7,
  input  D6,
  input  D5,
  input  D4,
  input  Sel3,
  output Output
);

  wire and_1_out, and_2_out, and_3_out, and_4_out, and_5_out, and_6_out, and_7_out, and_8_out, and_9_out,
       and_10_out, and_11_out, and_12_out, and_13_out, and_14_out, and_15_out, and_16_out, not_1_out,
       not_2_out, not_3_out, or_1_out, or_2_out;

  not not_1 (not_1_out, Sel3);
  not not_2 (not_2_out, Sel2);
  not not_3 (not_3_out, Sel1);
  and and_1 (and_1_out, Sel3, Sel2, Sel1);
  and and_2 (and_2_out, Sel3, Sel2, not_3_out);
  and and_3 (and_3_out, Sel3, not_2_out, Sel1);
  and and_4 (and_4_out, Sel3, not_2_out, not_3_out);
  and and_5 (and_5_out, not_1_out, Sel2, Sel1);
  and and_6 (and_6_out, not_1_out, Sel2, not_3_out);
  and and_7 (and_7_out, not_1_out, not_2_out, Sel1);
  and and_8 (and_8_out, not_1_out, not_2_out, not_3_out);
  and and_9 (and_9_out, D7, and_1_out);
  and and_10 (and_10_out, D6, and_2_out);
  and and_11 (and_11_out, D5, and_3_out);
  and and_12 (and_12_out, D4, and_4_out);
  and and_13 (and_13_out, D3, and_5_out);
  and and_14 (and_14_out, D2, and_6_out);
  and and_15 (and_15_out, D1, and_7_out);
  and and_16 (and_16_out, D0, and_8_out);
  or or_1 (or_1_out, and_13_out, and_14_out, and_15_out, and_16_out);
  or or_2 (or_2_out, and_9_out, and_10_out, and_11_out, and_12_out);
  or or_3 (Output, or_2_out, or_1_out);

  // Notes on the sheet:
  //   El presente circuito en un multiplexor de 8 entradas, 3 selectores y 1 salida. 
  //   Su funcionamiento consiste en solo dejar pasar el dato de entrada  del canal escogido,
  //   mediante la activación de los selectores Sel1, Sel2 y Sel3.
  //   Dicha selección se establece con los números binarios, por ejemplo, 
  //   si quiero dejar pasar el dato que se encuentre en D6, debo de poner el numero binario 110, 
  //   por lo que debo de activar Sel3, Sel2 y dejar inactivo Sel1.
  //    (Sel3 * 2**2) + (Sel2 * 2**1) + (Sel1 * 2**0)
endmodule
