// Digital circuit Ejercicio2.dig as structural Verilog
module Ejercicio2 (
  input  D0,
  input  Sel2,
  input  Sel1,
  output Output3,
  output Output2,
  output Output1,
  output Output0
);

  wire not_1_out, not_2_out;

  not not_1 (not_1_out, Sel2);
  not not_2 (not_2_out, Sel1);
  and and_1 (Output3, D0, Sel2, Sel1);
  and and_2 (Output2, D0, Sel2, not_2_out);
  and and_3 (Output1, D0, not_1_out, Sel1);
  and and_4 (Output0, D0, not_1_out, not_2_out);

  // Notes on the sheet:
  //   El funcionamiento del Demux es igual que el del Multiplexor, pero de manera inversa. 
  //   Este consta de 1 entrada, 4 salidas y 2 selectores. 
  //   Para poder escoger la salida se debe de realizar con los selectores. 
  //   Para elegir cual de las salidas se va a redirigir el dato de la entrada se debe de activar o desactivar los selectores.
endmodule
