// Digital circuit Ejercicio3_1.dig as structural Verilog
module Ejercicio3_1 (
  input  R,
  input  S,
  output Q,
  output Q_2
);

  nor nor_1 (Q, R, Q_2);
  nor nor_2 (Q_2, Q, S);

  // Notes on the sheet:
  //   1) Si su entrada Set se activa, el estado Q se pone en alto
  //   2) Si su entrada Reset se activa, el estado Q se pone en bajo
  //   3) Si no se activa ni Set ni Reset su estado Q no cambia
  //   4) No se permite activar Set y Reset simultáneamente
  //   El flip flop RS consta de dos entradas, R (reset) y S (set), y dos salidas, Q y Q’.
  //   Este flip flop en su variable Q es capaz de almacenar información. 
  //   El funcionamiento de este se explica a continuación:
endmodule
