// Digital circuit Ejercicio3_2.dig as structural Verilog
module Ejercicio3_2 (
  input  J,
  input  K,
  input  Clock,
  input  J_2,
  input  K_2,
  input  Clock_2,
  output Q,
  output Q_2,
  output Q_3,
  output Q_4
);

  wire nand_1_out, nand_2_out, nand_3_out, nand_4_out, nand_7_out, nand_8_out, nand_9_out, nand_10_out,
       not_1_out;

  nand nand_1 (nand_1_out, Q_2, J, Clock);
  nand nand_2 (nand_2_out, Clock, K, Q);
  nand nand_3 (nand_3_out, Q_4, J_2, Clock_2);
  nand nand_4 (nand_4_out, Clock_2, K_2, Q_3);
  not not_1 (not_1_out, Clock_2);
  nand nand_5 (Q, nand_1_out, Q_2);
  nand nand_6 (Q_2, Q, nand_2_out);
  nand nand_7 (nand_7_out, nand_3_out, nand_8_out);
  nand nand_8 (nand_8_out, nand_7_out, nand_4_out);
  nand nand_9 (nand_9_out, nand_7_out, not_1_out);
  nand nand_10 (nand_10_out, not_1_out, nand_8_out);
  nand nand_11 (Q_3, nand_9_out, Q_4);
  nand nand_12 (Q_4, Q_3, nand_10_out);

  // Notes on the sheet:
  //   El funcionamiento de este flip-flop es muy similar al flip-flop RS. Su funcionamiento se describe a continuación:
  //   1) Si J y K son diferentes la salida Q toma el valor de J durante la subida del siguiente pulso de reloj.
  //   2) Si J y K son cero, no se produce cambio alguno en la salida Q.
  //   Este flip-flop tiene el problema de que si el pulso de reloj se encuentra en subida y las entradas J y K se encuentran en 1, 
  //   el circuito comenzara a oscilar.
  //   Este problema se puede solucionar adicionando 4 NAND, este flip-flop se conoce como JK-Master-Slave.
  //   Este dispositivo se puede ver como dos flip-flops JK atados el uno al otro.
endmodule
