// Digital circuit Ejercicio4.dig as structural Verilog
module Ejercicio4 (
  input  \Configuración_1 ,
  input  Clock,
  input  Clear,
  input  Set,
  input  Estado_del_Pin_1,
  input  Enable,
  input  Estado_del_Pin_2,
  input  Estado_del_Pin_3,
  input  Estado_del_Pin_4,
  input  \Configuración_2 ,
  input  \Configuración_3 ,
  input  \Configuración_4 ,
  output \Registro_Configuración_1 ,
  output Registro_Almacenamiento_1,
  output Registro_Control_1,
  output \Registro_Configuración_2 ,
  output Registro_Almacenamiento_2,
  output Registro_Control_2,
  output \Registro_Configuración_3 ,
  output Registro_Almacenamiento_3,
  output Registro_Control_3,
  output \Registro_Configuración_4 ,
  output Registro_Almacenamiento_4,
  output Registro_Control_4
);

  wire Estado1, Estado_2, Estado_3, Estado_4, multiplexer_1_out, multiplexer_2_out, multiplexer_3_out,
       multiplexer_4_out, multiplexer_5_out, multiplexer_6_out, multiplexer_7_out, multiplexer_8_out;

  Multiplexer multiplexer_1 (
    .sel(Enable), .in_0(\Registro_Configuración_1 ), .in_1(\Configuración_1 ), .out(multiplexer_1_out));
  D_FF_AS d_ff_as_1 (
    .Set(Set), .D(multiplexer_1_out), .C(Clock), .Clr(Clear), .Q(\Registro_Configuración_1 ));  // open: nQ
  Multiplexer multiplexer_2 (.sel(Enable), .in_0(Estado1), .in_1(Estado_del_Pin_1), .out(multiplexer_2_out));
  D_FF_AS d_ff_as_2 (.Set(Set), .D(multiplexer_2_out), .C(Clock), .Clr(Clear), .Q(Estado1));  // open: nQ
  assign Registro_Control_1 = \Registro_Configuración_1  ? Estado1 : 1'bz;  // Driver driver_1
  assign Registro_Almacenamiento_1 = ~\Registro_Configuración_1  ? Estado1 : 1'bz;  // DriverInvSel driverinvsel_1
  Multiplexer multiplexer_3 (
    .sel(Enable), .in_0(\Registro_Configuración_2 ), .in_1(\Configuración_2 ), .out(multiplexer_3_out));
  Multiplexer multiplexer_4 (.sel(Enable), .in_0(Estado_2), .in_1(Estado_del_Pin_2), .out(multiplexer_4_out));
  D_FF_AS d_ff_as_3 (
    .Set(Set), .D(multiplexer_3_out), .C(Clock), .Clr(Clear), .Q(\Registro_Configuración_2 ));  // open: nQ
  D_FF_AS d_ff_as_4 (.Set(Set), .D(multiplexer_4_out), .C(Clock), .Clr(Clear), .Q(Estado_2));  // open: nQ
  assign Registro_Control_2 = \Registro_Configuración_2  ? Estado_2 : 1'bz;  // Driver driver_2
  assign Registro_Almacenamiento_2 = ~\Registro_Configuración_2  ? Estado_2 : 1'bz;  // DriverInvSel driverinvsel_2
  Multiplexer multiplexer_5 (.sel(Enable), .in_0(Estado_3), .in_1(Estado_del_Pin_3), .out(multiplexer_5_out));
  Multiplexer multiplexer_6 (
    .sel(Enable), .in_0(\Registro_Configuración_3 ), .in_1(\Configuración_3 ), .out(multiplexer_6_out));
  D_FF_AS d_ff_as_5 (.Set(Set), .D(multiplexer_5_out), .C(Clock), .Clr(Clear), .Q(Estado_3));  // open: nQ
  D_FF_AS d_ff_as_6 (
    .Set(Set), .D(multiplexer_6_out), .C(Clock), .Clr(Clear), .Q(\Registro_Configuración_3 ));  // open: nQ
  Multiplexer multiplexer_7 (.sel(Enable), .in_0(Estado_4), .in_1(Estado_del_Pin_4), .out(multiplexer_7_out));
  assign Registro_Control_3 = \Registro_Configuración_3  ? Estado_3 : 1'bz;  // Driver driver_3
  assign Registro_Almacenamiento_3 = ~\Registro_Configuración_3  ? Estado_3 : 1'bz;  // DriverInvSel driverinvsel_3
  D_FF_AS d_ff_as_7 (.Set(Set), .D(multiplexer_7_out), .C(Clock), .Clr(Clear), .Q(Estado_4));  // open: nQ
  Multiplexer multiplexer_8 (
    .sel(Enable), .in_0(\Registro_Configuración_4 ), .in_1(\Configuración_4 ), .out(multiplexer_8_out));
  D_FF_AS d_ff_as_8 (
    .Set(Set), .D(multiplexer_8_out), .C(Clock), .Clr(Clear), .Q(\Registro_Configuración_4 ));  // open: nQ
  assign Registro_Control_4 = \Registro_Configuración_4  ? Estado_4 : 1'bz;  // Driver driver_4
  assign Registro_Almacenamiento_4 = ~\Registro_Configuración_4  ? Estado_4 : 1'bz;  // DriverInvSel driverinvsel_4

  // Other names for the same wires on the sheet: In1 = Estado_del_Pin_1; In2 = Estado_del_Pin_2;
  //   In3 = Estado_del_Pin_3; In4 = Estado_del_Pin_4; RA1 = Registro_Almacenamiento_1;
  //   RA2 = Registro_Almacenamiento_2; RA3 = Registro_Almacenamiento_3; RA4 = Registro_Almacenamiento_4;
  //   RC1 = \Registro_Configuración_1 ; RC2 = \Registro_Configuración_2 ; RC3 = \Registro_Configuración_3 ;
  //   RC4 = \Registro_Configuración_4 ; RCN1 = Registro_Control_1; RCN2 = Registro_Control_2;
  //   RCN3 = Registro_Control_3; RCN4 = Registro_Control_4

  // Notes on the sheet:
  //   Registro_Configuración_1: Configuración, si es entrada (1) y si es salida (0)
  //   Registro_Almacenamiento_1: Almacena el estado del pin (si es un pin configurado como entrada)
  //   Registro_Control_1: Controla el estado del pin si fue configurado como una salida.
  //   Clock: Hz: 50
  //   Registro_Configuración_2: Configuración, si es entrada (1) y si es salida (0)
  //   Registro_Almacenamiento_2: Almacena el estado del pin (si es un pin configurado como entrada)
  //   Registro_Control_2: Controla el estado del pin si fue configurado como una salida.
  //   Registro_Configuración_3: Configuración, si es entrada (1) y si es salida (0)
  //   Registro_Almacenamiento_3: Almacena el estado del pin (si es un pin configurado como entrada)
  //   Registro_Control_3: Controla el estado del pin si fue configurado como una salida.
  //   Registro_Configuración_4: Configuración, si es entrada (1) y si es salida (0)
  //   Registro_Almacenamiento_4: Almacena el estado del pin (si es un pin configurado como entrada)
  //   Registro_Control_4: Controla el estado del pin si fue configurado como una salida.
  //   El registro DDR determina el comportamiento del pin si es una entrada o salida (1 salida, 0 entrada). 
  //   Este comportamiento se almacena en el “Registro de Configuración", el cual es de 4 bits.
  //   Si el comportamiento es “Salida” (1) -> el estado de los pines se almacenan en el “Registro de Control”, el cual es de 4 bits. 
  //   Si el comportamiento es “Entrada” (0) -> el estado de los pines se almacenan en el “Registro de Almacenamiento”, el cual es de 4 bits.
  //   Las entradas “Set” y “Clear” me permiten poner todos los bits de los pines en 1, si se activa “Set” o 0, si se activa “Clear”: 
  //   Set -> Comportamiento de los pines en “Salida” y estados de los pines en 1.
  //   Clear -> Comportamiento de los pines en “Entrada” y estados de los pines en 0.
  //   Para realizar el cambio de configuración de cada uno de los pines, se debe de activar el “Enable”, 
  //   este cambio se realiza activando o desactivando la entrada “Configuración #”, 
  //   el # corresponde al pin que se quiera cambiar, por ejemplo si es el pin 1 se debe de cambiar el estado de “Configuración 1”.
  //   Para realizar el cambio de estado de cada uno de los pines se debe activar el “Enable”, 
  //   para realizar el cambio de estado se debe activar o desactivar la entrada “Estado del Pin #”, 
  //   siendo # el número correspondiente al pin que se quiera cambiar, 
  //   por ejemplo si quiero cambiar el estado del pin 2 se debe cambiar el estado de “Estado del Pin 2”.
endmodule
